# Fritzing sketch door (saved by Fritzing 0.9.2b)
perfboards: 1

parts:
  Part2 = RFID-RC522-v2
  U2 = 2-Channel 5v Relay Shield [package=relay-2ch5v10a]
  S2 = Pushbutton [package=THT]
  Part3 = Arduino Wireless SD Shield

nets:
  N1: Part2.SDA, Part3.SD_CS
  N2: Part2.SCK, Part3.D5
  N3: Part2.MOSI, Part3.D7
  N4: Part2.MISO, Part3.D6
  GND: Part2.GND, U2.GND, Part3.GND
  N5: Part2.RST, Part3.D8
  3.3V: Part2.3.3V, Part3.3.3V
  VCC: U2.VCC, S2.leg0, Part3.+5V
  N6: U2.IN1, Part3.D2
  N7: S2.leg1, Part3.D3

custom parts:
  RFID-RC522-v2: A simple China made RFID-RC522 Reader; do check the pin labels, as this is a MFRC522 based clone.
  2-Channel 5v Relay Shield: 2 Channel 5v Relay Shield w. 2x SPD-06VDC-SD-C
